# Fritzing sketch StoniTenisShema (saved by Fritzing 0.9.10b)
breadboards: 1

parts:
  Banggood_Display1 = Banggood Display
  R1 = Rotary Potentiometer (Small) [maximum_resistance=100kΩ knob_status=50% power=0.5W package=THT]
  R2 = Rotary Potentiometer (Small) [maximum_resistance=100kΩ knob_status=50% power=0.5W package=THT]
  FRDM1 = Freescale FRDM KL25Z

nets:
  N1: Banggood_Display1.VCC, Banggood_Display1.LED
  N2: R1.leg1, R2.leg1
  N3: R1.leg2, R2.leg2
  N4: FRDM1.PTB1, FRDM1.PTC10, FRDM1.PTD5

custom parts:
  Freescale FRDM KL25Z: Freescale FRDM razvojni sistem
